# Fritzing sketch PlanMorze (saved by Fritzing 0.9.3b)

parts:
  R1 = Resistor [tolerance=±5% resistance=15k package=THT]
  LED1 = LED - 5mm [color="Green (560nm)" package="5 mm [THT]"]
  BC337-40 = NPN-Transistor [package="TO92 [THT]"]
  R2 = Resistor [tolerance=±5% resistance=470 package=THT]
  LED2 = LED - 5mm [color="Green (560nm)" package="5 mm [THT]"]
  LED3 = LED - 5mm [color="Green (560nm)" package="5 mm [THT]"]
  R3 = Resistor [tolerance=±5% resistance=15k package=THT]
  LED6 = LED - 5mm [color="Green (560nm)" package="5 mm [THT]"]
  LED7 = LED - 5mm [color="Green (560nm)" package="5 mm [THT]"]
  LED9 = LED - 5mm [color="Green (560nm)" package="5 mm [THT]"]
  LED10 = LED - 5mm [color="Green (560nm)" package="5 mm [THT]"]
  BC337-40_2 = NPN-Transistor [package="TO92 [THT]"]
  R4 = Resistor [tolerance=±5% resistance=330 package=THT]
  R5 = Resistor [tolerance=±5% resistance=15k package=THT]
  LED11 = LED - 5mm [color="Green (560nm)" package="5 mm [THT]"]
  LED12 = LED - 5mm [color="Green (560nm)" package="5 mm [THT]"]
  LED14 = LED - 5mm [color="Green (560nm)" package="5 mm [THT]"]
  LED15 = LED - 5mm [color="Green (560nm)" package="5 mm [THT]"]
  BC337-40_3 = NPN-Transistor [package="TO92 [THT]"]
  R6 = Resistor [tolerance=±5% resistance=330 package=THT]
  R7 = Resistor [tolerance=±5% resistance=15k package=THT]
  LED16 = LED - 5mm [color="Green (560nm)" package="5 mm [THT]"]
  LED17 = LED - 5mm [color="Green (560nm)" package="5 mm [THT]"]
  LED19 = LED - 5mm [color="Green (560nm)" package="5 mm [THT]"]
  LED20 = LED - 5mm [color="Green (560nm)" package="5 mm [THT]"]
  BC337-40_4 = NPN-Transistor [package="TO92 [THT]"]
  R8 = Resistor [tolerance=±5% resistance=330 package=THT]
  S1 = Square Pushbutton
  LED21 = RGB LED (com. cathode, rgb) [package="5 mm [THT]"]
  C1 = Ceramic Capacitor [capacitance=10nF package="100 mil [THT, multilayer]"]
  R9 = Resistor [tolerance=±5% resistance=220 package=THT]
  R10 = Resistor [tolerance=±5% resistance=220 package=THT]
  Part1 = Arduino Micro (Rev3)
  R11 = Resistor [tolerance=±5% resistance=15k package=THT]
  LED22 = LED - 5mm [color="Green (560nm)" package="5 mm [THT]"]
  LED23 = LED - 5mm [color="Green (560nm)" package="5 mm [THT]"]
  LED24 = LED - 5mm [color="Green (560nm)" package="5 mm [THT]"]
  LED25 = LED - 5mm [color="Green (560nm)" package="5 mm [THT]"]
  BC337-41 = NPN-Transistor [package="TO92 [THT]"]
  R12 = Resistor [tolerance=±5% resistance=330 package=THT]

nets:
  N1: R1.Pin_0, Part1.D10_PWM/A10
  N2: R1.Pin_1, BC337-40.B
  N3: LED1.cathode, R2.Pin_0
  N4: LED1.anode, LED2.cathode
  GND: BC337-40.E, BC337-40_2.E, BC337-40_3.E, BC337-40_4.E, S1.leg0, LED21.common_cathode, C1.0, BC337-41.E
  N5: BC337-40.C, R2.Pin_1
  N6: LED2.anode, LED3.cathode
  12V: LED3.anode, LED9.anode, LED14.anode, LED19.anode, LED22.anode
  N7: R3.Pin_0, Part1.D11_PWM
  N8: R3.Pin_1, BC337-40_2.B
  N9: LED6.cathode, LED7.anode
  N10: LED6.anode, LED10.cathode
  N11: LED7.cathode, R4.Pin_0
  N12: LED9.cathode, LED10.anode
  N13: BC337-40_2.C, R4.Pin_1
  N14: R5.Pin_0, Part1.D12_PWM/A11
  N15: R5.Pin_1, BC337-40_3.B
  N16: LED11.cathode, LED12.anode
  N17: LED11.anode, LED15.cathode
  N18: LED12.cathode, R6.Pin_0
  N19: LED14.cathode, LED15.anode
  N20: BC337-40_3.C, R6.Pin_1
  N21: R7.Pin_0, Part1.D13_PWM
  N22: R7.Pin_1, BC337-40_4.B
  N23: LED16.cathode, LED17.anode
  N24: LED16.anode, LED20.cathode
  N25: LED17.cathode, R8.Pin_0
  N26: LED19.cathode, LED20.anode
  N27: BC337-40_4.C, R8.Pin_1
  N28: S1.leg1, C1.1, Part1.D4_PWM/A6
  N29: LED21.red_anode, R10.Pin_1
  N30: LED21.blue_anode, R9.Pin_1
  N31: R9.Pin_0, Part1.D6_PWM/A7
  N32: R10.Pin_0, Part1.D5_PWM
  N33: Part1.D9_PWM/A9, R11.Pin_0
  N34: R11.Pin_1, BC337-41.B
  N35: LED22.cathode, LED23.anode
  N36: LED23.cathode, LED24.anode
  N37: LED24.cathode, LED25.anode
  N38: LED25.cathode, R12.Pin_0
  N39: BC337-41.C, R12.Pin_1
