# Fritzing sketch RU_02 (saved by Fritzing 0.9.3b)

parts:
  RU_02 = Arduino Micro (Rev3)
  Ethernet = Arduino Ethernet Shield (Rev3)
  R1 = Resistor [tolerance=±5% resistance=15k package="2010 [SMD]"]
  R2 = Resistor [tolerance=±5% resistance=2.2k package=THT]
  Q1 = NPN-Transistor [part_number=2n222 package="TO92 [THT]"]
  Q2 = NPN-Transistor [part_number=2n222 package="TO92 [THT]"]
  RED23 = LED - 5mm [color="Red (633nm)" package="5 mm [THT]"]
  GR23 = LED - 5mm [color="Green (565nm)" package="5 mm [THT]"]
  C1 = Ceramic Capacitor [capacitance=10nF package="100 mil [THT, multilayer]"]
  D1 = Schottky Diode [part_number=1N5817 breakdown_voltage=3.6V package="300 mil [THT]"]
  D2 = Schottky Diode [part_number=1N5817 breakdown_voltage=3.6V package="300 mil [THT]"]
  DD23 = Reed switch [package=THT]
  C2 = Ceramic Capacitor [capacitance=10nF package="100 mil [THT, multilayer]"]
  D3 = Schottky Diode [part_number=1N5817 breakdown_voltage=3.6V package="300 mil [THT]"]
  D4 = Schottky Diode [part_number=1N5817 breakdown_voltage=3.6V package="300 mil [THT]"]
  DDdpk = Reed switch [package=THT]
  PIR3 = PIR sensor
  PIR4 = PIR sensor
  DL23 = RELAY [package=relay-t9a]
  DLdpk = RELAY [package=relay-t9a]
  Key0Led = LED - 5mm [color="Green (560nm)" package="5 mm [THT]"]
  R5 = Resistor [tolerance=±5% resistance=220 package=THT]
  S1 = Square Pushbutton
  R6 = Resistor [tolerance=±5% resistance=10k package=THT]
  R7 = Resistor [tolerance=±5% resistance=10k package=THT]
  S2 = Square Pushbutton
  R8 = Resistor [tolerance=±5% resistance=10k package=THT]
  S3 = Square Pushbutton
  C3 = Ceramic Capacitor [capacitance=10nF package="100 mil [THT, multilayer]"]
  C4 = Ceramic Capacitor [capacitance=10nF package="100 mil [THT, multilayer]"]
  C5 = Ceramic Capacitor [capacitance=10nF package="100 mil [THT, multilayer]"]
  KEY0 = Square Pushbutton
  C6 = Ceramic Capacitor [capacitance=10nF package="100 mil [THT, multilayer]"]
  D14 = Schottky Diode [part_number=1N5817 breakdown_voltage=3.6V package="300 mil [THT]"]
  D15 = Schottky Diode [part_number=1N5817 breakdown_voltage=3.6V package="300 mil [THT]"]
  D13 = Rectifier Diode [part_number=1N4148 package="300 mil [THT]"]
  D12 = Rectifier Diode [part_number=1N4148 package="300 mil [THT]"]
  D11 = Rectifier Diode [part_number=1N4148 package="300 mil [THT]"]
  D10 = Rectifier Diode [part_number=1N4148 package="300 mil [THT]"]
  D9 = Rectifier Diode [part_number=1N4148 package="300 mil [THT]"]
  D8 = Rectifier Diode [part_number=1N4148 package="300 mil [THT]"]
  D7 = Rectifier Diode [part_number=1N4148 package="300 mil [THT]"]
  D6 = Rectifier Diode [part_number=1N4148 package="300 mil [THT]"]
  D5 = Rectifier Diode [part_number=1N4148 package="300 mil [THT]"]
  C7 = Ceramic Capacitor [capacitance=10nF package="100 mil [THT, multilayer]"]
  D16 = Schottky Diode [part_number=1N5817 breakdown_voltage=3.6V package="300 mil [THT]"]
  D17 = Schottky Diode [part_number=1N5817 breakdown_voltage=3.6V package="300 mil [THT]"]
  KEYBOX = Square Pushbutton
  Light/Alarm = RELAY [package=relay-t9a]

nets:
  N1: RU_02.MOSI, Ethernet.ICSP_MOSI
  N2: RU_02.D1/TX, Light/Alarm.COIL1
  N3: RU_02.D0/RX, C7.0, D16.anode, D17.cathode, KEYBOX.leg0
  GND: RU_02.GND, Ethernet.GND, Q1.E, Q2.E, C1.0, D2.anode, DD23.pin_2, C2.0, D4.anode, DDdpk.pin_2, DL23.COIL2, DLdpk.COIL2, Key0Led.cathode, R6.Pin_0, R7.Pin_0, R8.Pin_0, KEY0.leg1, C6.1, D15.anode, D11.anode, D8.anode, D5.anode, C7.1, D17.anode, KEYBOX.leg1, Light/Alarm.COIL2
  N4: RU_02.D2/SDA, R5.Pin_0
  N5: RU_02.D3/SCL, S1.leg0, R6.Pin_1, C3.0, D6.anode, D5.cathode
  N6: RU_02.D4_PWM/A6, S1.leg1, C3.1, D7.anode, D6.cathode
  N7: RU_02.D5_PWM, R7.Pin_1, S2.leg0, C4.0, D9.anode, D8.cathode
  N8: RU_02.D6_PWM/A7, S2.leg1, C4.1, D10.anode, D9.cathode
  N9: RU_02.D7, R8.Pin_1, S3.leg0, C5.0, D12.anode, D11.cathode
  N10: RU_02.D8_PWM/A8, S3.leg1, C5.1, D13.anode, D12.cathode
  N11: RU_02.D9_PWM/A9, KEY0.leg0, C6.0, D14.anode, D15.cathode
  N12: RU_02.D10_PWM/A10, Ethernet.ETH_CS
  N13: RU_02.D11_PWM, C2.1, D3.anode, D4.cathode, DDdpk.pin_1
  N14: RU_02.D12_PWM/A11, C1.1, D1.anode, D2.cathode, DD23.pin_1
  N15: RU_02.SCK, Ethernet.ICSP_SCK
  N16: RU_02.MISO, Ethernet.ICSP_MISO
  N17: RU_02.RESET, Ethernet.RESET
  5V: RU_02.5V, Ethernet.5V, D1.cathode, D3.cathode, D14.cathode, D13.cathode, D10.cathode, D7.cathode, D16.cathode
  N18: RU_02.A5, DLdpk.COIL1
  N19: RU_02.A4, DL23.COIL1
  N20: RU_02.A3, PIR4.SIG
  N21: RU_02.A2, PIR3.SIG
  N22: RU_02.A1, R1.Pin_0
  N23: RU_02.A0, R2.Pin_0
  N24: R1.Pin_1, Q1.B
  N25: R2.Pin_1, Q2.B
  N26: Q1.C, GR23.cathode
  N27: Q2.C, RED23.cathode
  12V: RED23.anode, GR23.anode
  N28: Key0Led.anode, R5.Pin_1
