# Fritzing sketch RU_05 (saved by Fritzing 0.9.3b)

parts:
  ETH = Arduino Ethernet Shield (Rev3)
  RU05 = Arduino Micro (Rev3)
  Nano = Arduino Nano (Rev3.0)
  NFC3 = RFID-RC522-v2
  NFC2 = RFID-RC522-v2
  NFC1 = RFID-RC522-v2
  M1 = DC Motor
  Q1 = Basic FET N-Channel [package="TO220 [THT]"]
  D1 = Rectifier Diode [part_number=1N4001 package="300 mil [THT]"]
  Hbridge-a = RELAY [package=relay-t9a]
  PIR5 = PIR sensor
  DDo = Toggle Switch [package=THT]
  DDc = Toggle Switch [package=THT]
  Hbridge-b = RELAY [package=relay-t9a]
  U1 = TOUCH [package=touch2]
  U2 = TOUCH [package=touch2]
  LED1 = LED - 5mm [color="Green (560nm)" package="5 mm [THT]"]
  R1 = Resistor [tolerance=±5% resistance=220 package=THT]
  LED2 = LED - 5mm [color="Green (560nm)" package="5 mm [THT]"]
  R2 = Resistor [tolerance=±5% resistance=220 package=THT]
  DLL = RELAY [package=relay-t9a]
  DLS = RELAY [package=relay-t9a]
  R3 = Resistor [tolerance=±5% resistance=10k package=THT]

nets:
  N1: ETH.ICSP_MISO, RU05.MISO
  N2: ETH.ICSP_SCK, RU05.SCK
  N3: ETH.ICSP_MOSI, RU05.MOSI
  N4: ETH.RESET, RU05.RESET
  N5: ETH.ETH_CS, RU05.D10_PWM/A10
  N6: RU05.D2/SDA, Nano.A4
  N7: RU05.D3/SCL, Nano.A5
  N8: RU05.D4_PWM/A6, DLL.COIL1
  N9: RU05.D5_PWM, DLS.COIL1
  N10: RU05.D8_PWM/A8, DDc.COM
  N11: RU05.D9_PWM/A9, DDo.COM
  N12: RU05.D11_PWM, Q1.gate, R3.Pin_1
  N13: RU05.D12_PWM/A11, Hbridge-a.COIL1, Hbridge-b.COIL1
  N14: RU05.A4, R2.Pin_1
  N15: RU05.A3, R1.Pin_1
  N16: RU05.A2, U1.T2
  N17: RU05.A1, U2.T2
  N18: RU05.A0, PIR5.SIG
  N19: Nano.D8, NFC1.IRQ
  N20: Nano.D9, NFC2.IRQ
  N21: Nano.D10, NFC3.IRQ
  N22: Nano.D11/MOSI, NFC3.MOSI, NFC2.MOSI, NFC1.MOSI
  N23: Nano.D12/MISO, NFC3.MISO, NFC2.MISO, NFC1.MISO
  N24: Nano.D13/SCK, NFC3.SCK, NFC2.SCK, NFC1.SCK
  N25: M1.pin_1, Hbridge-a.MAIN
  N26: M1.pin_2, Hbridge-b.MAIN
  N27: Q1.drain, D1.anode, Hbridge-a.NO, Hbridge-b.NC
  GND: Q1.source, Hbridge-a.COIL2, DDo.L2, DDc.L2, Hbridge-b.COIL2, R3.Pin_0
  12V: D1.cathode, Hbridge-a.NC, Hbridge-b.NO
  N28: LED1.anode, R1.Pin_0
  N29: LED2.anode, R2.Pin_0

custom parts:
  RFID-RC522-v2: A simple China made RFID-RC522 Reader; do check the pin labels, as this is a MFRC522 based clone.
