# Fritzing sketch RU_06 (saved by Fritzing 0.9.3b)

parts:
  ETH = Arduino Ethernet Shield (Rev3)
  RU06 = Arduino Micro (Rev3)
  Часть3 = Arduino Nano (Rev3.0)
  NFC6 = RFID-RC522-v2
  NFC5 = RFID-RC522-v2
  NFC4 = RFID-RC522-v2
  DLp1 = RELAY [package=relay-t9a]
  PIR6 = PIR sensor
  DLp2 = RELAY [package=relay-t9a]
  DLven = RELAY [package=relay-t9a]
  DLL2 = RELAY [package=relay-t9a]
  DLL1 = RELAY [package=relay-t9a]
  DLL0 = RELAY [package=relay-t9a]
  R7 = Resistor [tolerance=±5% resistance=10k package=THT]
  C4 = Ceramic Capacitor [capacitance=10nF package="100 mil [THT, multilayer]"]
  D8 = Rectifier Diode [part_number=1N4148 package="300 mil [THT]"]
  D9 = Rectifier Diode [part_number=1N4148 package="300 mil [THT]"]
  D10 = Rectifier Diode [part_number=1N4148 package="300 mil [THT]"]
  S2 = Square Pushbutton

nets:
  N1: ETH.ICSP_MISO, RU06.MISO
  N2: ETH.ICSP_SCK, RU06.SCK
  N3: ETH.ICSP_MOSI, RU06.MOSI
  N4: ETH.RESET, RU06.RESET
  N5: ETH.ETH_CS, RU06.D10_PWM/A10
  N6: RU06.D2/SDA, Часть3.A4
  N7: RU06.D3/SCL, Часть3.A5
  N8: RU06.D4_PWM/A6, R7.Pin_1, C4.0, D9.anode, D10.cathode, S2.leg0
  N9: RU06.D5_PWM, C4.1, D8.anode, D9.cathode, S2.leg1
  N10: RU06.D12_PWM/A11, PIR6.SIG
  N11: RU06.A5, DLL0.COIL1
  N12: RU06.A4, DLL1.COIL1
  N13: RU06.A3, DLL2.COIL1
  N14: RU06.A2, DLven.COIL1
  N15: RU06.A1, DLp2.COIL1
  N16: RU06.A0, DLp1.COIL1
  N17: Часть3.D8, NFC4.IRQ
  N18: Часть3.D9, NFC5.IRQ
  N19: Часть3.D10, NFC6.IRQ
  N20: Часть3.D11/MOSI, NFC6.MOSI, NFC5.MOSI, NFC4.MOSI
  N21: Часть3.D12/MISO, NFC6.MISO, NFC5.MISO, NFC4.MISO
  N22: Часть3.D13/SCK, NFC6.SCK, NFC5.SCK, NFC4.SCK
  GND: R7.Pin_0, D10.anode
  5V: D8.cathode

custom parts:
  RFID-RC522-v2: A simple China made RFID-RC522 Reader; do check the pin labels, as this is a MFRC522 based clone.
