# Fritzing sketch USB_box (saved by Fritzing 0.9.2b)
circuit board: 8.46667cm x 5.64444cm

parts:
  Segment1 = 7 Segment Display
  Segment4 = 7 Segment Display
  Segment3 = 7 Segment Display
  Segment2 = 7 Segment Display
  Q9 = PNP-Transistor [package="TO92 [THT]"]
  Q10 = PNP-Transistor [package="TO92 [THT]"]
  Q11 = PNP-Transistor [package="TO92 [THT]"]
  Q12 = PNP-Transistor [package="TO92 [THT]"]
  Q1 = NPN-Transistor [package="TO92 [THT]"]
  Q3 = NPN-Transistor [package="TO92 [THT]"]
  Q7 = NPN-Transistor [package="TO92 [THT]"]
  Q8 = NPN-Transistor [package="TO92 [THT]"]
  Q6 = NPN-Transistor [package="TO92 [THT]"]
  Q5 = NPN-Transistor [package="TO92 [THT]"]
  Q4 = NPN-Transistor [package="TO92 [THT]"]
  Q2 = NPN-Transistor [package="TO92 [THT]"]
  R1 = Resistor [tolerance=±5% resistance=68 package=THT]
  R2 = Resistor [tolerance=±5% resistance=68 package=THT]
  R3 = Resistor [tolerance=±5% resistance=68 package=THT]
  R4 = Resistor [tolerance=±5% resistance=68 package=THT]
  R5 = Resistor [tolerance=±5% resistance=68 package=THT]
  R6 = Resistor [tolerance=±5% resistance=68 package=THT]
  R7 = Resistor [tolerance=±5% resistance=68 package=THT]
  R8 = Resistor [tolerance=±5% resistance=68 package=THT]
  R9 = Resistor [tolerance=±5% resistance=15k package=THT]
  R10 = Resistor [tolerance=±5% resistance=15k package=THT]
  R11 = Resistor [tolerance=±5% resistance=15k package=THT]
  R12 = Resistor [tolerance=±5% resistance=15k package=THT]
  R13 = Resistor [tolerance=±5% resistance=15k package=THT]
  R14 = Resistor [tolerance=±5% resistance=15k package=THT]
  R15 = Resistor [tolerance=±5% resistance=15k package=THT]
  R16 = Resistor [tolerance=±5% resistance=15k package=THT]
  R17 = Resistor [tolerance=±5% resistance=15k package=THT]
  R18 = Resistor [tolerance=±5% resistance=15k package=THT]
  R19 = Resistor [tolerance=±5% resistance=15k package=THT]
  R20 = Resistor [tolerance=±5% resistance=15k package=THT]
  MU1 = Arduino Nano (Rev3.0)
  S1 = Round Pushbutton
  LED1 = LED - 3mm [color="Green (560nm)" package="3 mm [THT]"]
  R21 = Resistor [tolerance=±5% resistance=150 package=THT]
  R22 = Resistor [tolerance=±5% resistance=10k package=THT]
  Q13 = NPN-Transistor [package="TO92 [THT]"]
  X1 = USB Connectors [package=usb-a-s-nosilk-female]
  D1 = Schottky Diode [part_number=1N5817 package="Melf DO-213 AB [SMD]"]
  D2 = Schottky Diode [part_number=1N5817 package="Melf DO-213 AB [SMD]"]
  D3 = Schottky Diode [part_number=1N5817 package="Melf DO-213 AB [SMD]"]

nets:
  N1: Segment1.Segment_E, Segment4.Segment_E, Segment3.Segment_E, Segment2.Segment_E, R5.Pin_1
  N2: Segment1.Segment_D, Segment4.Segment_D, Segment3.Segment_D, Segment2.Segment_D, R4.Pin_1
  N3: Segment1.common_anode, Q9.C
  N4: Segment1.Segment_C, Segment4.Segment_C, Segment3.Segment_C, Segment2.Segment_C, R3.Pin_1
  N5: Segment1.Segment_DP, Segment4.Segment_DP, Segment3.Segment_DP, Segment2.Segment_DP, R8.Pin_1
  N6: Segment1.Segment_B, Segment4.Segment_B, Segment3.Segment_B, Segment2.Segment_B, R2.Pin_1
  N7: Segment1.Segment_A, Segment4.Segment_A, Segment3.Segment_A, Segment2.Segment_A, R1.Pin_1
  N8: Segment1.Segment_F, Segment4.Segment_F, Segment3.Segment_F, Segment2.Segment_F, R6.Pin_1
  N9: Segment1.Segment_G, Segment4.Segment_G, Segment3.Segment_G, Segment2.Segment_G, R7.Pin_1
  N10: Segment4.common_anode, Q12.C
  N11: Segment3.common_anode, Q11.C
  N12: Segment2.common_anode, Q10.C
  5V: Q9.E, Q10.E, Q11.E, Q12.E, MU1.5V, X1.D+, D3.cathode
  N13: Q9.B, R9.Pin_1
  N14: Q10.B, R10.Pin_1
  N15: Q11.B, R12.Pin_1
  N16: Q12.B, R11.Pin_1
  GND: Q1.E, Q3.E, Q7.E, Q8.E, Q6.E, Q5.E, Q4.E, Q2.E, MU1.GND, S1.leg0, LED1.cathode, X1.GND, D1.anode
  N17: Q1.B, R13.Pin_1
  N18: Q1.C, R1.Pin_0
  N19: Q3.B, R15.Pin_1
  N20: Q3.C, R3.Pin_0
  N21: Q7.B, R19.Pin_1
  N22: Q7.C, R7.Pin_0
  N23: Q8.B, R20.Pin_1
  N24: Q8.C, R8.Pin_0
  N25: Q6.B, R18.Pin_1
  N26: Q6.C, R6.Pin_0
  N27: Q5.B, R17.Pin_1
  N28: Q5.C, R5.Pin_0
  N29: Q4.B, R16.Pin_1
  N30: Q4.C, R4.Pin_0
  N31: Q2.B, R14.Pin_1
  N32: Q2.C, R2.Pin_0
  N33: R9.Pin_0, MU1.A0
  N34: R10.Pin_0, MU1.A1
  N35: R11.Pin_0, MU1.A3
  N36: R12.Pin_0, MU1.A2
  N37: R13.Pin_0, MU1.D2
  N38: R14.Pin_0, MU1.D3
  N39: R15.Pin_0, MU1.D4
  N40: R16.Pin_0, MU1.D5
  N41: R17.Pin_0, MU1.D6
  N42: R18.Pin_0, MU1.D7
  N43: R19.Pin_0, MU1.D8
  N44: R20.Pin_0, MU1.D9
  N45: MU1.D10, R22.Pin_1
  N46: MU1.A5, R21.Pin_1
  N47: MU1.A4, S1.leg1
  N48: LED1.anode, R21.Pin_0
  N49: R22.Pin_0, Q13.B
  N50: Q13.E, X1.VBUS, D1.cathode, D2.anode
  N51: Q13.C, X1.D-, D2.cathode, D3.anode
