# Fritzing sketch USB_box_v.2 (saved by Fritzing 0.9.2b)

parts:
  MU1 = Arduino Nano (Rev3.0)
  S1 = Round Pushbutton
  LED1 = LED - 3mm [color="Green (560nm)" package="3 mm [THT]"]
  R21 = Resistor [tolerance=±5% resistance=150 package=THT]
  R22 = Resistor [tolerance=±5% resistance=10k package=THT]
  Q13 = NPN-Transistor [package="TO92 [THT]"]
  X1 = USB Connectors [package=usb-a-s-nosilk-female]
  D1 = Schottky Diode [part_number=1N5817 package="Melf DO-213 AB [SMD]"]
  D2 = Schottky Diode [part_number=1N5817 package="Melf DO-213 AB [SMD]"]
  D3 = Schottky Diode [part_number=1N5817 package="Melf DO-213 AB [SMD]"]
  U1 = 7-SEGMENT-4DIGIT [package=7-segment-4digit_longpads_for_pogobed]

nets:
  GND: MU1.GND, S1.leg0, LED1.cathode, X1.GND, D1.anode
  N1: MU1.D2, U1.2
  N2: MU1.D3, U1.1
  N3: MU1.D10, R22.Pin_1
  N4: MU1.A5, R21.Pin_1
  N5: MU1.A4, S1.leg1
  N6: LED1.anode, R21.Pin_0
  N7: R22.Pin_0, Q13.B
  N8: Q13.E, X1.VBUS, D1.cathode, D2.anode
  N9: Q13.C, X1.D-, D2.cathode, D3.anode
  5V: X1.D+, D3.cathode
